// Logisim project BitFixo.circ as structural Verilog: 1 circuit, main circuit main
module main (
  input  in_1,
  input  BIT,
  input  in_3,
  output out_4,
  output out_5,
  output out_6
);

  wire and_1_out, and_3_out, not_1_out, not_2_out, not_3_out, or_2_out;

  and and_1 (and_1_out, in_1, not_1_out);
  not not_1 (not_1_out, in_1);
  not not_2 (not_2_out, in_3);
  or or_1 (out_4, in_1, and_1_out);
  and and_2 (out_6, in_3, or_2_out);
  or or_2 (or_2_out, in_3, not_2_out);
  not not_3 (not_3_out, BIT);
  and and_3 (and_3_out, BIT, not_3_out);
  xor xor_1 (out_5, BIT, and_3_out);

  // Notes on the sheet:
  //   BIT
  //   BIT
  //   OR <BIT>, 0
  //   1
  //   AND <BIT>, 1
  //   0
  //   Mantem o valor
  //   Mantem o valor
  //   XOR <BIT>, 0
  //   0
  //   Mantem o valor
endmodule
