// Logisim project Operadores.circ as structural Verilog: 7 circuits, main circuit ANDBits
module ANDBits (
  input  Operando,
  input  Operador,
  output Saida
);

  and and_1 (Saida, Operando, Operador);
endmodule

module ORBits (
  input  Operando,
  input  Operador,
  output Saida
);

  or or_1 (Saida, Operando, Operador);
endmodule

module XORBits (
  input  Operando,
  input  Operador,
  output Saida
);

  xor xor_1 (Saida, Operando, Operador);
endmodule

module OPAnd (
  input  [7:0] Operando,
  input  [7:0] Operador,
  output [7:0] Resultado
);

  ANDBits andbits_1 (.Operando(Operando[0]), .Operador(Operador[0]), .Saida(Resultado[0]));
  ANDBits andbits_2 (.Operando(Operando[1]), .Operador(Operador[1]), .Saida(Resultado[1]));
  ANDBits andbits_3 (.Operando(Operando[2]), .Operador(Operador[2]), .Saida(Resultado[2]));
  ANDBits andbits_4 (.Operando(Operando[3]), .Operador(Operador[3]), .Saida(Resultado[3]));
  ANDBits andbits_5 (.Operando(Operando[4]), .Operador(Operador[4]), .Saida(Resultado[4]));
  ANDBits andbits_6 (.Operando(Operando[5]), .Operador(Operador[5]), .Saida(Resultado[5]));
  ANDBits andbits_7 (.Operando(Operando[6]), .Operador(Operador[6]), .Saida(Resultado[6]));
  ANDBits andbits_8 (.Operando(Operando[7]), .Operador(Operador[7]), .Saida(Resultado[7]));
endmodule

module OPOr (
  input  [7:0] Operando,
  input  [7:0] Operador,
  output [7:0] Resultado
);

  ORBits orbits_1 (.Operando(Operando[0]), .Operador(Operador[0]), .Saida(Resultado[0]));
  ORBits orbits_2 (.Operando(Operando[1]), .Operador(Operador[1]), .Saida(Resultado[1]));
  ORBits orbits_3 (.Operando(Operando[2]), .Operador(Operador[2]), .Saida(Resultado[2]));
  ORBits orbits_4 (.Operando(Operando[3]), .Operador(Operador[3]), .Saida(Resultado[3]));
  ORBits orbits_5 (.Operando(Operando[4]), .Operador(Operador[4]), .Saida(Resultado[4]));
  ORBits orbits_6 (.Operando(Operando[5]), .Operador(Operador[5]), .Saida(Resultado[5]));
  ORBits orbits_7 (.Operando(Operando[6]), .Operador(Operador[6]), .Saida(Resultado[6]));
  ORBits orbits_8 (.Operando(Operando[7]), .Operador(Operador[7]), .Saida(Resultado[7]));
endmodule

module OPXor (
  input  [7:0] Operando,
  input  [7:0] Operador,
  output [7:0] Resultado
);

  XORBits xorbits_1 (.Operando(Operando[0]), .Operador(Operador[0]), .Saida(Resultado[0]));
  XORBits xorbits_2 (.Operando(Operando[1]), .Operador(Operador[1]), .Saida(Resultado[1]));
  XORBits xorbits_3 (.Operando(Operando[2]), .Operador(Operador[2]), .Saida(Resultado[2]));
  XORBits xorbits_4 (.Operando(Operando[3]), .Operador(Operador[3]), .Saida(Resultado[3]));
  XORBits xorbits_5 (.Operando(Operando[4]), .Operador(Operador[4]), .Saida(Resultado[4]));
  XORBits xorbits_6 (.Operando(Operando[5]), .Operador(Operador[5]), .Saida(Resultado[5]));
  XORBits xorbits_7 (.Operando(Operando[6]), .Operador(Operador[6]), .Saida(Resultado[6]));
  XORBits xorbits_8 (.Operando(Operando[7]), .Operador(Operador[7]), .Saida(Resultado[7]));
endmodule

module Main (
  input  [7:0] in_1,
  input  [7:0] in_2,
  output [7:0] out_3,
  output [7:0] out_4,
  output [7:0] out_5
);

  OPAnd opand_1 (.Operando(in_1), .Operador(in_2), .Resultado(out_3));
  OPOr opor_1 (.Operando(in_1), .Operador(in_2), .Resultado(out_4));
  OPXor opxor_1 (.Operando(in_1), .Operador(in_2), .Resultado(out_5));

  // Notes on the sheet:
  //   Operando
  //   Operador
  //   And Operando, Operador
  //   Or Operando, Operador
  //   Xor Operando, Operador
endmodule
