// Logisim project Tecprog.circ as structural Verilog: 1 circuit, main circuit main
module main (
  input  in_1,
  input  in_2,
  input  in_3,
  output out_4,
  output out_5,
  output out_6
);

  wire and_2_out, not_1_out, not_2_out, not_3_out, or_1_out, or_3_out;

  or or_1 (or_1_out, in_1, not_1_out);
  not not_1 (not_1_out, in_1);
  not not_2 (not_2_out, in_3);
  or or_2 (out_4, in_1, or_1_out);
  and and_1 (out_6, in_3, and_2_out);
  and and_2 (and_2_out, in_3, not_2_out);
  not not_3 (not_3_out, in_2);
  or or_3 (or_3_out, in_2, not_3_out);
  xor xor_1 (out_5, in_2, or_3_out);

  // Notes on the sheet:
  //   BIT
  //   BIT
  //   OR <BIT>, 1
  //   1
  //   AND <BIT>, 0
  //   0
  //   Mantem sempre 1
  //   Mantem sempre 0
  //   BIT
  //   XOR <BIT>, 1
  //   Inverte o valor
endmodule
